// Logisim project Lab8_ALU_PC.circ as structural Verilog: 1 circuit, main circuit main
module main (
  input  [3:0] A,
  input  [3:0] B,
  input  Mode,
  input  EN,
  input  RST,
  output [3:0] Result,
  output Carry_Borrow,
  output [3:0] PC
);

  wire Bsub, Cadd, CLK;
  wire [3:0] adder_1_out, DIFF, SUM;

  Clock u_CLK (.out(CLK));
  Adder #(.width(4)) adder_1 (.a(PC), .b(4'b0001), .out(adder_1_out), .cin(1'b0));  // open: cout
  Adder #(.width(4)) adder_2 (.a(A), .b(B), .out(SUM), .cin(1'b0), .cout(Cadd));
  Subtractor #(.width(4)) subtractor_1 (.a(A), .b(B), .out(DIFF), .bin(1'b0), .bout(Bsub));
  // Register #(.width(4)) PCreg: pin names not known; wires that end beside it: adder_1_out, EN
  Multiplexer #(.width(4)) multiplexer_1 (.in0(SUM), .in1(DIFF), .out(Result), .sel(Mode));  // open: en
  Multiplexer multiplexer_2 (.in0(Cadd), .in1(Bsub), .out(Carry_Borrow), .sel(Mode));  // open: en

  // Other names for the same wires on the sheet: M = Mode; PCQ[3:0] = PC

  // Notes on the sheet:
  //   4-BIT MINI-ALU  (Mode = 0 : A + B   |   Mode = 1 : A - B)
  //   4-BIT PROGRAM COUNTER  (D flip-flop register + incrementer, with Enable and Reset)
  //   c = a + b;  ->  ALU (Mode=0) adds registers a and b
  //   for(i=0;i<8;i++)  ->  PC (register) + 1 each clock
  //   i is held in flip-flops (Register), +1 by the adder
endmodule
