// Logisim project Lab_6.circ as structural Verilog: 5 circuits, main circuit Fig2_Mod60_Counter
module Fig1a_DFF_Register_Bit (
  input  Din,
  input  EN,
  input  RST,
  output Q
);

  wire CLK_out, multiplexer_1_out;

  Clock CLK (.out(CLK_out));
  Multiplexer multiplexer_1 (.in0(Q), .in1(Din), .out(multiplexer_1_out), .en(EN));  // open: sel
  D_Flip_Flop d_ff_1 (.clk(multiplexer_1_out), .D(CLK_out), .Q(Q), .en(RST));  // open: Qn, preset, reset
endmodule

module Fig1b_Keypad_Debounce (
  input  KEY,
  input  RST,
  output Q2,
  output Y,
  output Q1
);

  wire SCLK;

  Clock u_SCLK (.out(SCLK));
  D_Flip_Flop d_ff_1 (.clk(KEY), .D(SCLK), .Q(Q1), .en(RST));  // open: Qn, preset, reset
  D_Flip_Flop d_ff_2 (.clk(Q1), .D(SCLK), .Q(Q2), .en(RST));  // open: Qn, preset, reset
  and and_1 (Y, Q1, Q2);
endmodule

module Fig2_Mod60_Counter (
  input  RST,
  output Q0,
  output Q1,
  output Q2,
  output Q3,
  output Q4,
  output Q5,
  output TC
);

  wire and_7_out, and_8_out, and_9_out, and_10_out, and_11_out, and_12_out, CLK, Qn2, T2, T3, T4, T5, TCa,
       TCb, TCc, xor_1_out, xor_2_out, xor_3_out, xor_4_out, xor_5_out;

  Clock u_CLK (.out(CLK));
  and and_1 (T2, Q1, Q0);
  and and_2 (T3, Q2, T2);
  and and_3 (T4, Q3, T3);
  and and_4 (T5, Q4, T4);
  and and_5 (TCa, Qn2, T2);
  xor xor_1 (xor_1_out, Q1, Q0);
  xor xor_2 (xor_2_out, Q2, T2);
  xor xor_3 (xor_3_out, Q3, T3);
  xor xor_4 (xor_4_out, Q4, T4);
  xor xor_5 (xor_5_out, Q5, T5);
  and and_6 (TCb, TCa, Q3);
  and and_7 (and_7_out, ~Q0, ~TC);  // AND_Gate
  and and_8 (and_8_out, xor_1_out, ~TC);  // AND_Gate
  and and_9 (and_9_out, xor_2_out, ~TC);  // AND_Gate
  and and_10 (and_10_out, xor_3_out, ~TC);  // AND_Gate
  and and_11 (and_11_out, xor_4_out, ~TC);  // AND_Gate
  and and_12 (and_12_out, xor_5_out, ~TC);  // AND_Gate
  D_Flip_Flop d_ff_1 (.clk(and_7_out), .D(CLK), .Q(Q0), .en(RST));  // open: Qn, preset, reset
  D_Flip_Flop d_ff_2 (.clk(and_8_out), .D(CLK), .Q(Q1), .en(RST));  // open: Qn, preset, reset
  D_Flip_Flop d_ff_3 (.clk(and_9_out), .D(CLK), .Q(Q2), .Qn(Qn2), .en(RST));  // open: preset, reset
  D_Flip_Flop d_ff_4 (.clk(and_10_out), .D(CLK), .Q(Q3), .en(RST));  // open: Qn, preset, reset
  D_Flip_Flop d_ff_5 (.clk(and_11_out), .D(CLK), .Q(Q4), .en(RST));  // open: Qn, preset, reset
  D_Flip_Flop d_ff_6 (.clk(and_12_out), .D(CLK), .Q(Q5), .en(RST));  // open: Qn, preset, reset
  and and_13 (TCc, TCb, Q4);
  and and_14 (TC, TCc, Q5);
endmodule

module Fig3a_SIPO_Shift_Register (
  input  SI,
  input  RST,
  output Q0,
  output Q1,
  output Q2,
  output Q3
);

  wire CLK;

  Clock u_CLK (.out(CLK));
  D_Flip_Flop d_ff_1 (.clk(SI), .D(CLK), .Q(Q0), .en(RST));  // open: Qn, preset, reset
  D_Flip_Flop d_ff_2 (.clk(Q0), .D(CLK), .Q(Q1), .en(RST));  // open: Qn, preset, reset
  D_Flip_Flop d_ff_3 (.clk(Q1), .D(CLK), .Q(Q2), .en(RST));  // open: Qn, preset, reset
  D_Flip_Flop d_ff_4 (.clk(Q2), .D(CLK), .Q(Q3), .en(RST));  // open: Qn, preset, reset
endmodule

module Fig3b_PISO_Shift_Register (
  input  P3,
  input  P2,
  input  P1,
  input  P0,
  input  LOAD,
  input  SI,
  input  RST,
  output Q3,
  output Q2,
  output Q1,
  output Q0,
  output SO
);

  wire CLK, multiplexer_1_out, multiplexer_2_out, multiplexer_3_out, multiplexer_4_out;

  Clock u_CLK (.out(CLK));
  Multiplexer multiplexer_1 (.in0(SI), .in1(P3), .out(multiplexer_1_out), .en(LOAD));  // open: sel
  D_Flip_Flop d_ff_1 (.clk(multiplexer_1_out), .D(CLK), .Q(Q3), .en(RST));  // open: Qn, preset, reset
  Multiplexer multiplexer_2 (.in0(Q3), .in1(P2), .out(multiplexer_2_out), .en(LOAD));  // open: sel
  D_Flip_Flop d_ff_2 (.clk(multiplexer_2_out), .D(CLK), .Q(Q2), .en(RST));  // open: Qn, preset, reset
  Multiplexer multiplexer_3 (.in0(Q2), .in1(P1), .out(multiplexer_3_out), .en(LOAD));  // open: sel
  D_Flip_Flop d_ff_3 (.clk(multiplexer_3_out), .D(CLK), .Q(Q1), .en(RST));  // open: Qn, preset, reset
  Multiplexer multiplexer_4 (.in0(Q1), .in1(P0), .out(multiplexer_4_out), .en(LOAD));  // open: sel
  D_Flip_Flop d_ff_4 (.clk(multiplexer_4_out), .D(CLK), .Q(Q0), .en(RST));  // open: Qn, preset, reset

  assign SO = Q0;
endmodule
